# Fritzing sketch jwnode (saved by Fritzing 0.9.3b)
breadboards: 1

parts:
  Part1 = Arduino Uno (Rev3)
  Part2 = Bluetooth HC-05 Macho
  R1 = Resistor [tolerance=±5% resistance=330 package=THT]
  LED1 = LED - 5mm [color="Blue (505nm)" package="5 mm [THT]"]
  U1 = NodeMCU V1.0

nets:
  5V: Part1.5V, Part2.VCC
  GND: Part1.GND, Part2.GND, R1.Pin_0, U1.GND
  N1: Part2.TXD, U1.RX
  N2: Part2.RXD, U1.TX
  N3: R1.Pin_1, LED1.anode
  N4: LED1.cathode, U1.D2

notes:
  Plug the HC-05 in, the short green wires are only pointing to which holes they go in.

custom parts:
  NodeMCU V1.0: ESP8266 based NodeMCU
